// Logisim project ALU.circ as structural Verilog: 1 circuit, main circuit main
module main (
  input  [15:0] A,
  input  [15:0] B,
  input  ALU,
  output [15:0] result
);

  wire [15:0] adder_1_out, and_1_out;

  Adder #(.width(16)) adder_1 (.a(A), .b(B), .out(adder_1_out));  // open: cin, cout
  assign and_1_out = A & B;  // AND_Gate and_1, 16 bits wide
  Multiplexer #(.width(16)) multiplexer_1 (.in0(adder_1_out), .in1(and_1_out), .out(result), .sel(ALU), .en(ALU));
endmodule
