// Logisim project LAB TASK.circ as structural Verilog: 1 circuit, main circuit ALU
module ALU (
  input  [15:0] A,
  input  [15:0] B,
  input  [1:0] ALU_SEL,
  output [15:0] R
);

  wire [15:0] and_1_out, or_1_out, subtractor_1_out;

  Subtractor #(.width(16)) subtractor_1 (.a(A), .b(B), .out(subtractor_1_out));  // open: bin, bout
  Adder #(.width(16)) adder_1 (.a(A), .b(B), .out(subtractor_1_out));  // open: cin, cout
  assign or_1_out = A | B;  // OR_Gate or_1, 16 bits wide
  assign and_1_out = A & B;  // AND_Gate and_1, 16 bits wide
  Multiplexer #(.select(2), .width(16)) multiplexer_1 (
    .in0(subtractor_1_out), .in1(subtractor_1_out), .in2(or_1_out), .in3(and_1_out), .out(R), .sel(ALU_SEL));  // open: en
endmodule
